// Logisim project ESF.circ as structural Verilog: 2 circuits, main circuit main
module main (
  input  [31:0] in_1,
  input  [15:0] in_2,
  input  [31:0] in_3,
  input  [31:0] in_4,
  input  [31:0] in_5,
  input  [3:0] in_6,
  input  in_7,
  input  in_8,
  input  [4:0] in_9,
  input  [4:0] in_10,
  output [4:0] out_11,
  output [31:0] out_12,
  output [31:0] out_13
);

  wire and_2_out, clock_1_out, not_5_out, or_2_out;
  wire [0:0] not_3_out;
  wire [4:0] adder_1_out, and_1_out, not_4_out, or_1_out;
  wire [15:0] main_2_out_6, multiplexer_5_out, register_3_q;
  wire [31:0] main_1_out_3, main_2_out_7, main_2_out_8, multiplexer_1_out, multiplexer_3_out,
       multiplexer_4_out, not_1_out, not_2_out, register_1_q, register_2_q, register_4_q, register_5_q,
       shift7_1_out_2;

  assign not_1_out = ~in_1;  // NOT_Gate not_1, 32 bits wide
  Multiplexer #(.width(32)) multiplexer_1 (
    .in0(not_1_out), .in1(register_2_q), .out(multiplexer_1_out), .sel(or_2_out));  // open: en
  shift7 shift7_1 (.in_1(multiplexer_1_out), .out_2(shift7_1_out_2));
  Register #(.width(32)) register_1 (.D(out_13), .en(not_5_out), .Q(register_1_q), .clk(clock_1_out));  // open: clr
  assign out_13 = shift7_1_out_2 ^ main_1_out_3;  // XOR_Gate xor_1, 32 bits wide
  RoundFunction_main main_1 (.in_1(out_12), .in_2(multiplexer_3_out), .out_3(main_1_out_3));
  Register #(.width(32)) register_2 (.D(out_12), .en(not_5_out), .Q(register_2_q), .clk(clock_1_out));  // open: clr
  assign not_2_out = ~in_3;  // NOT_Gate not_2, 32 bits wide
  Multiplexer #(.width(32)) multiplexer_2 (
    .in0(not_2_out), .in1(register_1_q), .out(out_12), .sel(or_2_out));  // open: en
  Clock clock_1 (.out(clock_1_out));
  not not_3 (not_3_out[0], in_7);
  Counter #(.width(5), .max('h1f)) counter_1 (
    .load(in_8), .count(not_5_out), .Q(out_11), .clk(clock_1_out));  // open: D, carry, clr
  assign or_1_out = out_11 | in_9;  // OR_Gate or_1, 5 bits wide
  or or_2 (or_2_out, or_1_out[4], or_1_out[3], or_1_out[2], or_1_out[1], or_1_out[0]);
  Multiplexer #(.width(32)) multiplexer_3 (
    .in0(in_4), .in1(register_5_q), .out(multiplexer_3_out), .sel(or_2_out));  // open: en
  Multiplexer #(.width(32)) multiplexer_4 (
    .in0(in_5), .in1(register_4_q), .out(multiplexer_4_out), .sel(or_2_out));  // open: en
  esfKeyT_main main_2 (
    .in_2(in_8), .in_5(multiplexer_3_out), .in_3(multiplexer_4_out), .in_1(multiplexer_5_out),
    .out_8(main_2_out_8), .out_7(main_2_out_7), .out_6(main_2_out_6), .counter(adder_1_out));
  assign and_1_out = out_11 & not_4_out;  // AND_Gate and_1, 5 bits wide
  Multiplexer #(.width(16)) multiplexer_5 (
    .in0(in_2), .in1(register_3_q), .out(multiplexer_5_out), .sel(or_2_out));  // open: en
  Adder #(.width(5)) adder_1 (.a(out_11), .b({in_6, not_3_out[0]}), .out(adder_1_out));  // open: cin, cout
  assign not_4_out = ~in_10;  // NOT_Gate not_4, 5 bits wide
  and and_2 (and_2_out, and_1_out[4], and_1_out[3], and_1_out[2], and_1_out[1], and_1_out[0]);
  not not_5 (not_5_out, and_2_out);
  Register #(.width(16)) register_3 (
    .D(main_2_out_6), .en(not_5_out), .Q(register_3_q), .clk(clock_1_out));  // open: clr
  Register #(.width(32)) register_4 (
    .D(main_2_out_7), .en(not_5_out), .Q(register_4_q), .clk(clock_1_out));  // open: clr
  Register #(.width(32)) register_5 (
    .D(main_2_out_8), .en(not_5_out), .Q(register_5_q), .clk(clock_1_out));  // open: clr

  // Notes on the sheet:
  //   L_0
  //   R_0
  //   key
endmodule

module shift7 (
  input  [31:0] in_1,
  output [31:0] out_2
);


  assign out_2 = {in_1[24:0], in_1[31:25]};
endmodule
