// Logisim project PRESENT.circ as structural Verilog: 5 circuits, main circuit main
module main (
  input  [15:0] in_1,
  input  [31:0] in_2,
  input  [31:0] in_3,
  input  [31:0] in_4,
  input  [31:0] in_5,
  input  [3:0] key_transform,
  input  in_7,
  input  in_8,
  input  [4:0] in_9,
  input  [4:0] in_10,
  input  in_11,
  input  in_12,
  input  in_13,
  input  in_14,
  output [4:0] out_15,
  output [31:0] out_16
);

  wire and_2_out, clock_1_out, clock_2_out, not_2_out, not_4_out, or_2_out, undriven, undriven_2;
  wire [0:0] not_1_out;
  wire [2:0] counter_1_q;
  wire [4:0] adder_1_out, and_1_out, not_3_out, or_1_out;
  wire [15:0] keyt_1_out_6, multiplexer_3_out, register_5_q;
  wire [31:0] buffer_1_out, counter_2_q, keyt_1_out_5, keyt_1_out_7, multiplexer_1_out, multiplexer_2_out,
       multiplexer_4_out, multiplexer_5_out, register_1_q, register_2_q, register_3_q, register_4_q,
       selectkey_1_out_4, selectkey_1_out_5, selectkey_2_out_4, selectkey_2_out_5, spnet_1_out_3,
       spnet_1_out_4, xor_1_out, xor_2_out, xor_3_out, xor_4_out;

  Register #(.width(32)) register_1 (.D(xor_2_out), .en(not_4_out), .Q(register_1_q), .clk(clock_2_out));  // open: clr
  assign xor_1_out = in_2 ^ selectkey_1_out_4;  // XOR_Gate xor_1, 32 bits wide
  Multiplexer #(.width(32)) multiplexer_1 (
    .in0(xor_1_out), .in1(register_1_q), .out(multiplexer_1_out), .sel(or_2_out));  // open: en
  assign xor_2_out = spnet_1_out_3 ^ selectkey_2_out_4;  // XOR_Gate xor_2, 32 bits wide
  assign xor_3_out = in_3 ^ selectkey_1_out_5;  // XOR_Gate xor_3, 32 bits wide
  Multiplexer #(.width(32)) multiplexer_2 (
    .in0(xor_3_out), .in1(register_2_q), .out(multiplexer_2_out), .sel(or_2_out));  // open: en
  SPNet spnet_1 (.in_2(multiplexer_1_out), .in_1(multiplexer_2_out), .out_3(spnet_1_out_3), .out_4(spnet_1_out_4));
  Counter #(.width(3), .max('h7)) counter_1 (
    .count(in_11), .Q(counter_1_q), .clk(clock_1_out));  // open: load, D, carry, clr
  Counter #(.width(32), .max('hffffffff)) counter_2 (
    .load(in_11), .count(in_12), .Q(counter_2_q), .clk(clock_1_out));  // open: D, carry, clr
  assign xor_4_out = spnet_1_out_4 ^ selectkey_2_out_5;  // XOR_Gate xor_4, 32 bits wide
  SelectKey selectkey_1 (.in_3(in_1), .in_1(in_4), .in_2(in_5), .out_4(selectkey_1_out_4), .out_5(selectkey_1_out_5));
  SelectKey selectkey_2 (
    .in_3(keyt_1_out_6), .in_1(keyt_1_out_5), .in_2(keyt_1_out_7), .out_4(selectkey_2_out_4),
    .out_5(selectkey_2_out_5));
  Register #(.width(32)) register_2 (.D(xor_4_out), .en(not_4_out), .Q(register_2_q), .clk(clock_2_out));  // open: clr
  assign buffer_1_out = counter_2_q;  // Buffer buffer_1, 32 bits wide
  Clock clock_1 (.out(clock_1_out));
  Multiplexer #(.width(16)) multiplexer_3 (
    .in0(in_1), .in1(register_5_q), .out(multiplexer_3_out), .sel(or_2_out), .en(undriven));
  Counter #(.width(5), .max('h1f)) counter_3 (
    .load(in_8), .count(not_4_out), .Q(out_15), .clk(clock_2_out));  // open: D, carry, clr
  Clock clock_2 (.out(clock_2_out));
  not not_1 (not_1_out[0], in_7);
  assign or_1_out = out_15 | in_9;  // OR_Gate or_1, 5 bits wide
  or or_2 (or_2_out, or_1_out[4], or_1_out[3], or_1_out[2], or_1_out[1], or_1_out[0]);
  RAM #(.addrWidth(3), .dataWidth(32), .bus("separate")) ram_1 (
    .addr(counter_1_q), .din(buffer_1_out), .data(out_16), .str(clock_1_out), .sel(in_13), .clk(clock_1_out),
    .ld(not_2_out), .clr(in_14));
  not not_2 (not_2_out, clock_1_out);
  Multiplexer #(.width(32)) multiplexer_4 (
    .in0(in_4), .in1(register_4_q), .out(multiplexer_4_out), .sel(or_2_out));  // open: en
  KeyT keyt_1 (
    .in_1(multiplexer_3_out), .in_2(multiplexer_4_out), .in_3(multiplexer_5_out), .out_6(keyt_1_out_6),
    .out_5(keyt_1_out_5), .out_7(keyt_1_out_7), .counter(adder_1_out));
  Multiplexer #(.width(32)) multiplexer_5 (
    .in0(in_5), .in1(register_3_q), .out(multiplexer_5_out), .sel(or_2_out), .en(undriven_2));
  Adder #(.width(5)) adder_1 (.a(out_15), .b({key_transform, not_1_out[0]}), .out(adder_1_out));  // open: cin, cout
  Register #(.width(32)) register_3 (
    .D(keyt_1_out_7), .en(not_4_out), .Q(register_3_q), .clk(clock_2_out));  // open: clr
  assign and_1_out = out_15 & not_3_out;  // AND_Gate and_1, 5 bits wide
  Register #(.width(32)) register_4 (
    .D(keyt_1_out_5), .en(not_4_out), .Q(register_4_q), .clk(clock_2_out));  // open: clr
  assign not_3_out = ~in_10;  // NOT_Gate not_3, 5 bits wide
  and and_2 (and_2_out, and_1_out[4], and_1_out[3], and_1_out[2], and_1_out[1], and_1_out[0]);
  not not_4 (not_4_out, and_2_out);
  Register #(.width(16)) register_5 (
    .D(keyt_1_out_6), .en(not_4_out), .Q(register_5_q), .clk(clock_2_out));  // open: clr

  // Notes on the sheet:
  //   out_16: pull=down
  //   add Round Key
  //   add Round Key
  //   sp layer
  //   select Key
  //   select Key
  //   ticks enable
  //   remove this at the end
  //   when str and sel is 1 then value at west edge is transferred to the RAM
  //   when ld and sel is 1 then value from selected address goes into east side D
  //   select line control signal
endmodule

module Sbox (
  input  msb_to_lsb,
  input  in_2,
  input  in_3,
  input  in_4,
  output out_5,
  output out_6,
  output out_7,
  output out_8
);

  wire and_1_out, and_2_out, and_3_out, and_4_out, and_5_out, and_6_out, and_7_out, and_8_out, and_9_out,
       and_10_out, and_11_out, and_12_out, and_13_out, and_14_out, and_15_out, and_16_out, and_17_out,
       and_18_out, and_19_out, and_20_out, and_21_out, not_1_out, not_2_out, not_3_out, not_4_out;

  not not_1 (not_1_out, msb_to_lsb);
  not not_2 (not_2_out, in_2);
  not not_3 (not_3_out, in_3);
  not not_4 (not_4_out, in_4);
  and and_1 (and_1_out, not_4_out, not_3_out, not_1_out);
  and and_2 (and_2_out, not_1_out, in_3, in_4);
  and and_3 (and_3_out, not_1_out, not_4_out, in_2);
  and and_4 (and_4_out, msb_to_lsb, not_2_out, in_4);
  and and_5 (and_5_out, msb_to_lsb, not_2_out, in_3);
  and and_6 (and_6_out, not_2_out, in_3, not_4_out);
  and and_7 (and_7_out, msb_to_lsb, in_2, not_3_out);
  and and_8 (and_8_out, in_2, in_3, in_4, not_1_out);
  and and_9 (and_9_out, not_1_out, not_2_out, in_3);
  and and_10 (and_10_out, not_1_out, in_3, not_4_out);
  and and_11 (and_11_out, not_2_out, in_3, not_4_out);
  and and_12 (and_12_out, msb_to_lsb, not_2_out, not_3_out);
  and and_13 (and_13_out, msb_to_lsb, in_2, in_4);
  and and_14 (and_14_out, not_1_out, not_2_out, in_4);
  and and_15 (and_15_out, not_1_out, in_3, in_4);
  and and_16 (and_16_out, msb_to_lsb, not_2_out, not_4_out);
  and and_17 (and_17_out, msb_to_lsb, in_3, not_4_out);
  and and_18 (and_18_out, not_1_out, not_2_out, not_3_out);
  or or_1 (out_5, and_1_out, and_2_out, and_3_out, and_4_out, and_5_out);
  and and_19 (and_19_out, and_3_out, not_3_out);
  and and_20 (and_20_out, and_7_out, in_4);
  and and_21 (and_21_out, not_2_out, not_3_out, in_4);
  or or_2 (out_6, and_21_out, and_18_out, and_6_out, and_7_out, and_8_out);
  or or_3 (out_7, and_9_out, and_10_out, and_11_out, and_12_out, and_13_out);
  or or_4 (out_8, and_14_out, and_15_out, and_16_out, and_19_out, and_17_out, and_20_out);

  // Notes on the sheet:
  //   gives B1
  //   gives B3
  //   gives B2
  //   overall B
  //   gives B4
  //   B1-B4
  //   B1 is most significant
endmodule

module SPNet (
  input  [31:0] in_1,
  input  [31:0] in_2,
  output [31:0] out_3,
  output [31:0] out_4
);

  Sbox sbox_1 (
    .msb_to_lsb(in_2[31]), .in_2(in_2[30]), .in_3(in_2[29]), .in_4(in_2[28]), .out_5(out_3[31]),
    .out_6(out_3[15]), .out_7(out_4[31]), .out_8(out_4[15]));
  Sbox sbox_2 (
    .msb_to_lsb(in_2[27]), .in_2(in_2[26]), .in_3(in_2[25]), .in_4(in_2[24]), .out_5(out_3[30]),
    .out_6(out_3[14]), .out_7(out_4[30]), .out_8(out_4[14]));
  Sbox sbox_3 (
    .msb_to_lsb(in_2[23]), .in_2(in_2[22]), .in_3(in_2[21]), .in_4(in_2[20]), .out_5(out_3[29]),
    .out_6(out_3[13]), .out_7(out_4[29]), .out_8(out_4[13]));
  Sbox sbox_4 (
    .msb_to_lsb(in_2[19]), .in_2(in_2[18]), .in_3(in_2[17]), .in_4(in_2[16]), .out_5(out_3[28]),
    .out_6(out_3[12]), .out_7(out_4[28]), .out_8(out_4[12]));
  Sbox sbox_5 (
    .msb_to_lsb(in_2[15]), .in_2(in_2[14]), .in_3(in_2[13]), .in_4(in_2[12]), .out_5(out_3[27]),
    .out_6(out_3[11]), .out_7(out_4[27]), .out_8(out_4[11]));
  Sbox sbox_6 (
    .msb_to_lsb(in_2[11]), .in_2(in_2[10]), .in_3(in_2[9]), .in_4(in_2[8]), .out_5(out_3[26]),
    .out_6(out_3[10]), .out_7(out_4[26]), .out_8(out_4[10]));
  Sbox sbox_7 (
    .msb_to_lsb(in_2[7]), .in_2(in_2[6]), .in_3(in_2[5]), .in_4(in_2[4]), .out_5(out_3[25]),
    .out_6(out_3[9]), .out_7(out_4[25]), .out_8(out_4[9]));
  Sbox sbox_8 (
    .msb_to_lsb(in_2[3]), .in_2(in_2[2]), .in_3(in_2[1]), .in_4(in_2[0]), .out_5(out_3[24]),
    .out_6(out_3[8]), .out_7(out_4[24]), .out_8(out_4[8]));
  Sbox sbox_9 (
    .msb_to_lsb(in_1[31]), .in_2(in_1[30]), .in_3(in_1[29]), .in_4(in_1[28]), .out_5(out_3[23]),
    .out_6(out_3[7]), .out_7(out_4[23]), .out_8(out_4[7]));
  Sbox sbox_10 (
    .msb_to_lsb(in_1[27]), .in_2(in_1[26]), .in_3(in_1[25]), .in_4(in_1[24]), .out_5(out_3[22]),
    .out_6(out_3[6]), .out_7(out_4[22]), .out_8(out_4[6]));
  Sbox sbox_11 (
    .msb_to_lsb(in_1[19]), .in_2(in_1[18]), .in_3(in_1[17]), .in_4(in_1[16]), .out_5(out_3[20]),
    .out_6(out_3[4]), .out_7(out_4[20]), .out_8(out_4[4]));
  Sbox sbox_12 (
    .msb_to_lsb(in_1[23]), .in_2(in_1[22]), .in_3(in_1[21]), .in_4(in_1[20]), .out_5(out_3[21]),
    .out_6(out_3[5]), .out_7(out_4[21]), .out_8(out_4[5]));
  Sbox sbox_13 (
    .msb_to_lsb(in_1[15]), .in_2(in_1[14]), .in_3(in_1[13]), .in_4(in_1[12]), .out_5(out_3[19]),
    .out_6(out_3[3]), .out_7(out_4[19]), .out_8(out_4[3]));
  Sbox sbox_14 (
    .msb_to_lsb(in_1[11]), .in_2(in_1[10]), .in_3(in_1[9]), .in_4(in_1[8]), .out_5(out_3[18]),
    .out_6(out_3[2]), .out_7(out_4[18]), .out_8(out_4[2]));
  Sbox sbox_15 (
    .msb_to_lsb(in_1[3]), .in_2(in_1[2]), .in_3(in_1[1]), .in_4(in_1[0]), .out_5(out_3[16]),
    .out_6(out_3[0]), .out_7(out_4[16]), .out_8(out_4[0]));
  Sbox sbox_16 (
    .msb_to_lsb(in_1[7]), .in_2(in_1[6]), .in_3(in_1[5]), .in_4(in_1[4]), .out_5(out_3[17]),
    .out_6(out_3[1]), .out_7(out_4[17]), .out_8(out_4[1]));

  // Notes on the sheet:
  //   48
  //   48
  //   16
  //   32
  //   32
  //   0
  //   16
  //   16
  //   0
endmodule

module KeyT (
  input  [15:0] in_1,
  input  [31:0] in_2,
  input  [31:0] in_3,
  input  [4:0] counter,
  output [31:0] out_5,
  output [15:0] out_6,
  output [31:0] out_7
);

  Sbox sbox_1 (
    .msb_to_lsb(in_3[18]), .in_2(in_3[17]), .in_3(in_3[16]), .in_4(in_3[15]), .out_5(out_6[15]),
    .out_6(out_6[14]), .out_7(out_6[13]), .out_8(out_6[12]));
  assign out_7[19:15] = in_2[6:2] ^ counter;  // XOR_Gate xor_1, 5 bits wide

  assign out_5 = {in_3[2:0], in_1, in_2[31:19]};
  assign out_6[11:0] = in_3[14:3];
  assign {out_7[31:20], out_7[14:0]} = {in_2[18:7], in_2[1:0], in_3[31:19]};

  // Notes on the sheet:
  //   msb
  //   lsb
  //   19
  //   15
endmodule

module SelectKey (
  input  [31:0] in_1,
  input  [31:0] in_2,
  input  [15:0] in_3,
  output [31:0] out_4,
  output [31:0] out_5
);


  assign out_4 = {in_3, in_1[31:16]};
  assign out_5 = {in_1[15:0], in_2[31:16]};

  // Notes on the sheet:
  //   80 bit Key
  //   msb
  //   lsb 
endmodule
